# Fritzing sketch neouti (saved by Fritzing 0.9.3b)
breadboards: 1

parts:
  U1 = RMCM01 [package=rmcm01]
  Part1 = Arduino Uno (Rev3) - ICSP
  U2 = NodeMCU V1.0
  T1 = LM35 Temperature Sensor [package="TO92 [THT]"]
  Part2 = Adafruit MAX4466 Electret Microphone Amplifier [part_number="Adafruit #1063"]
  R1 = Resistor [tolerance=±5% resistance=10k package=THT]
  R2 = Resistor [tolerance=±5% resistance=10k package=THT]
  R3 = Resistor [tolerance=±5% resistance=220 package=THT]
  LED1 = LED - 5mm [color="Green (555nm)" package="5 mm [THT]"]
  LED2 = LED - 5mm [color="Red (633nm)" package="5 mm [THT]"]
  R4 = Resistor [tolerance=±5% resistance=220 package=THT]

nets:
  VCC: U1.VCC, Part1.3V3, Part2.VCC, R1.Pin_1, R2.Pin_1
  N1: U1.SCL, Part1.A4/SDA, R1.Pin_0
  N2: U1.SDA, Part1.A5/SCL, R2.Pin_0
  N3: Part1.A0, Part2.OUT
  N4: Part1.A1, T1.Vout
  GND: Part1.GND, U2.GND, T1.GND, Part2.GND, R3.Pin_1, R4.Pin_1
  N5: Part1.D3_PWM, U2.RX
  N6: Part1.5V, T1.+Vs
  N7: U2.D1, LED1.anode
  N8: U2.D2, LED2.anode
  N9: R3.Pin_0, LED1.cathode
  N10: LED2.cathode, R4.Pin_0

custom parts:
  RMCM01: Polar Heart Rate Monitor module
  NodeMCU V1.0: ESP8266 based NodeMCU
  Adafruit MAX4466 Electret Microphone Amplifier: Add an ear to your project with this well-designed electret microphone amplifier. This fully assembled and tested board comes with a 20-20KHz electret microphone soldered on. For the amplification, we use the Maxim MAX4466, an op-amp specifically designed for this delicate task! The amplifier has excellent power supply noise rejection, so this amplifier sounds really good and isn't nearly as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
